# Fritzing sketch Prototype_Basic (saved by Fritzing 0.9.3b)
breadboards: 1

parts:
  Bauteil1 = Arduino Nano (Rev3.0)
  S1 = Momentary Switch [package=ksa_sealed_tac_switch]
  LED1 = smd LED [color="Red (633nm)" package="0603 [SMD]"]
  R1 = Resistor [tolerance=±1% resistance=10k package="0402 [SMD]"]
  R2 = Resistor [tolerance=±1% resistance=220 package="0402 [SMD]"]
  S2 = Momentary Switch [package=ksa_sealed_tac_switch]
  R3 = Resistor [tolerance=±1% resistance=10k package="0402 [SMD]"]
  S3 = Momentary Switch [package=ksa_sealed_tac_switch]
  LED3 = smd LED [color="Red (633nm)" package="0603 [SMD]"]
  R5 = Resistor [tolerance=±1% resistance=10k package="0402 [SMD]"]
  R6 = Resistor [tolerance=±1% resistance=220 package="0402 [SMD]"]
  U1 = 4-Channel 5v Relay Shield [package=relay-4ch5v10a]
  Bauteil2 = ENC28J60 Breakout Board
  U2 = SWITCH_SPDT [package=kps-1290]

nets:
  N1: Bauteil1.RESET, Bauteil2.RESET
  GND: Bauteil1.GND, LED1.anode, R1.Pin_1, R3.Pin_1, LED3.anode, R5.Pin_1, U1.GND, Bauteil2.GND
  N2: Bauteil1.D2, S2.4
  N3: Bauteil1.D3, R2.Pin_0
  N4: Bauteil1.D4, S1.4
  N5: Bauteil1.D5, R6.Pin_0
  N6: Bauteil1.D6, S3.4
  N7: Bauteil1.D7, U1.IN1, U1.IN2
  N8: Bauteil1.D8, Bauteil2.CS
  N9: Bauteil1.D9, U1.IN3
  N10: Bauteil1.D11/MOSI, Bauteil2.SI
  N11: Bauteil1.D12/MISO, Bauteil2.SO
  N12: Bauteil1.VIN, U2.O
  3V3: Bauteil1.3V3, Bauteil2.VCC
  N13: Bauteil1.D13/SCK, Bauteil2.SCK
  N14: S1.1, S2.1, S3.1, U1.VCC, U2.P
  N15: S1.3, R1.Pin_0
  N16: LED1.cathode, R2.Pin_1
  N17: S2.3, R3.Pin_0
  N18: S3.3, R5.Pin_0
  N19: LED3.cathode, R6.Pin_1
  N20: U1.K1-On, U1.K3-Off

notes:
  open
  close
  230V in
  5V in

custom parts:
  4-Channel 5v Relay Shield: 4 Channel 5v Relay Shield w. 2x SPD-06VDC-SD-C
  ENC28J60 Breakout Board: This is a breakout board for the Microchip ENC28J60 stand-alone ethernet controller. The ENC28J60 has an SPI interface. It operates at 3.3 Volts.

// code stored in the sketch: sketch.ino
#include "etherShield.h"
#include "ETHER_28J60.h"
 
static uint8_t mac[6] = {0x54, 0x55, 0x58, 0x10, 0x00, 0x24};   
static uint8_t ip[4] = {192, 168, 1, 15};                      
static uint16_t port = 80;                                    
 
ETHER_28J60 ethernet;
 
void setup()
{ 
  ethernet.setup(mac, ip, port);
}
 
void loop()
{
  if (ethernet.serviceRequest())
  {
    ethernet.print("<H1>Hello World</H1>");
    ethernet.respond();
  }
  delay(100);
}
